// Logisim project 2Mux.circ as structural Verilog: 2 circuits, main circuit 2:1 Mux
module _2_1_Mux (
  input  S,
  input  I0,
  input  I1,
  output Y
);

  wire and_1_out, and_2_out, not_1_out;

  not not_1 (not_1_out, S);
  and and_1 (and_1_out, I0, not_1_out);
  and and_2 (and_2_out, I1, S);
  or or_1 (Y, and_1_out, and_2_out);

  // Notes on the sheet:
  //   2:1 Mux
endmodule

module _4_1_Mux (
  input  I0,
  input  I1,
  input  I2,
  input  I3,
  input  S0,
  input  S1,
  input  in_7,
  input  in_8,
  input  in_9,
  input  in_10,
  input  in_11,
  input  in_12,
  output out_13,
  output out_14
);

  wire n2_1_mux_1_y, n2_1_mux_2_y, not_2_out;

  _2_1_Mux u_2_1_mux_1 (.S(S0), .I0(I0), .I1(I1), .Y(n2_1_mux_1_y));
  _2_1_Mux u_2_1_mux_2 (.S(S0), .I0(I2), .I1(I3), .Y(n2_1_mux_2_y));
  _2_1_Mux u_2_1_mux_3 (.S(S1), .I0(n2_1_mux_1_y), .I1(n2_1_mux_2_y), .Y(out_13));
  // NOT_Gate not_1 has open pins: in=in_7, out=open
  not not_2 (not_2_out, in_8);
  // AND_Gate and_1 is placed but not wired
  // AND_Gate and_2 is placed but not wired
  // AND_Gate and_3 has open pins: in0=in_11, in1=in_7, in2=not_2_out, out=open
  // AND_Gate and_4 has open pins: in0=in_12, in1=in_7, in2=in_8, out=open
  // OR_Gate or_1 is placed but not wired
endmodule
