// Logisim project 4bit RCA_2.circ as structural Verilog: 3 circuits, main circuit main
module main (
  input  a,
  input  b,
  output sum,
  output cout
);

  xor xor_1 (sum, a, b);
  and and_1 (cout, a, b);

  // Notes on the sheet:
  //   Half Adder
endmodule

module FA (
  input  a,
  input  b,
  input  cin,
  output sum,
  output cout
);

  wire main_1_cout, main_1_sum, main_2_cout;

  main main_1 (.a(a), .b(b), .sum(main_1_sum), .cout(main_1_cout));
  main main_2 (.a(main_1_sum), .b(cin), .sum(sum), .cout(main_2_cout));
  or or_1 (cout, main_1_cout, main_2_cout);

  // Notes on the sheet:
  //   Full Adder
endmodule

module Ripple_carry_adder (
  input  [3:0] a,
  input  in_2,
  input  [3:0] b,
  output C4,
  output S3,
  output S2,
  output S1,
  output S0,
  output [4:0] out_9
);

  wire fa_2_cout, fa_3_cout, fa_4_cout;

  FA fa_1 (.a(a[3]), .b(b[3]), .cin(fa_2_cout), .sum(S3), .cout(C4));
  FA fa_2 (.a(a[2]), .b(b[2]), .cin(fa_3_cout), .sum(S2), .cout(fa_2_cout));
  FA fa_3 (.a(a[1]), .b(b[1]), .cin(fa_4_cout), .sum(S1), .cout(fa_3_cout));
  FA fa_4 (.a(a[0]), .b(b[0]), .cin(in_2), .sum(S0), .cout(fa_4_cout));

  // Other names for the same wires on the sheet: S0_t = out_9[0]; S1_t = out_9[1]; S2_t = out_9[2]; S3_t = out_9[3];
  //   C4_t = out_9[4]

  // Notes on the sheet:
  //   Ripple Carry Adder
endmodule
