// Logisim project Reg_file_2.circ as structural Verilog: 4 circuits, main circuit main
module main (
  input  [3:0] Din,
  input  Clk,
  input  En,
  output [3:0] Dout
);

  D_Flip_Flop d_ff_1 (.clk(Clk), .D(Din[0]), .Q(Dout[0]), .en(En));  // open: Qn, preset, reset
  D_Flip_Flop d_ff_2 (.clk(Clk), .D(Din[1]), .Q(Dout[1]), .en(En));  // open: Qn, preset, reset
  D_Flip_Flop d_ff_3 (.clk(Clk), .D(Din[2]), .Q(Dout[2]), .en(En));  // open: Qn, preset, reset
  D_Flip_Flop d_ff_4 (.clk(Clk), .D(Din[3]), .Q(Dout[3]), .en(En));  // open: Qn, preset, reset
endmodule

module reg_file (
  input  [3:0] Din,
  input  m2_sel,
  input  Din_2,
  input  [1:0] Mux_sel,
  input  den,
  input  [1:0] sel,
  output [3:0] out_7,
  output [3:0] out_8,
  output [3:0] out_9,
  output [3:0] out_10,
  output [3:0] out_11
);

  wire clock_1_out, decoder_1_out0, decoder_1_out1, decoder_1_out2, decoder_1_out3;
  wire [3:0] multiplexer_1_out;

  Multiplexer #(.width(4), .enable("false")) multiplexer_1 (
    .in0(out_9), .in1(Din), .out(multiplexer_1_out), .sel(m2_sel));
  main R0 (.Din(multiplexer_1_out), .Dout(out_7), .Clk(clock_1_out), .En(decoder_1_out0));
  main R1 (.Din(multiplexer_1_out), .Dout(out_8), .Clk(clock_1_out), .En(decoder_1_out1));
  main R2 (.Din(multiplexer_1_out), .Dout(out_10), .Clk(clock_1_out), .En(decoder_1_out2));
  main R3 (.Din(multiplexer_1_out), .Dout(out_11), .Clk(clock_1_out), .En(decoder_1_out3));
  Clock clock_1 (.out(clock_1_out));
  Decoder #(.select(2)) decoder_1 (
    .out0(decoder_1_out0), .out1(decoder_1_out1), .out2(decoder_1_out2), .out3(decoder_1_out3), .sel(sel),
    .en(den));
  Multiplexer #(.select(2), .width(4)) multiplexer_2 (
    .in0(out_7), .in1(out_8), .in2(out_10), .in3(out_11), .out(out_9), .sel(Mux_sel), .en(Din_2));
endmodule

module _8_bit_reg (
  input  [7:0] Din,
  input  Clk,
  input  En,
  output [7:0] out_4
);

  main main_1 (.Din(Din[3:0]), .Dout(out_4[3:0]), .Clk(Clk), .En(En));
  main main_2 (.Din(Din[7:4]), .Dout(out_4[7:4]), .Clk(Clk), .En(En));
endmodule

module _8_bit_reg_file (
  input  [7:0] Din,
  input  [7:0] in_2,
  input  [7:0] in_3,
  input  [7:0] in_4,
  input  [7:0] in_5,
  input  [7:0] in_6,
  input  [2:0] in_7,
  input  [7:0] in_8,
  input  [7:0] in_9,
  input  [7:0] in_10,
  input  Clk,
  input  [2:0] in_12,
  input  en,
  output [7:0] out_14
);

  wire decoder_1_out0, decoder_1_out1, decoder_1_out2, decoder_1_out3, decoder_1_out4, decoder_1_out5,
       decoder_1_out6, decoder_1_out7;

  _8_bit_reg u_8_bit_reg_1 (.Din(Din), .out_4(in_2), .Clk(Clk), .En(decoder_1_out0));
  _8_bit_reg u_8_bit_reg_2 (.Din(Din), .out_4(in_3), .Clk(Clk), .En(decoder_1_out1));
  _8_bit_reg u_8_bit_reg_3 (.Din(Din), .out_4(in_4), .Clk(Clk), .En(decoder_1_out2));
  _8_bit_reg u_8_bit_reg_4 (.Din(Din), .out_4(in_5), .Clk(Clk), .En(decoder_1_out3));
  _8_bit_reg u_8_bit_reg_5 (.Din(Din), .out_4(in_6), .Clk(Clk), .En(decoder_1_out4));
  _8_bit_reg u_8_bit_reg_6 (.Din(Din), .out_4(in_8), .Clk(Clk), .En(decoder_1_out5));
  _8_bit_reg u_8_bit_reg_7 (.Din(Din), .out_4(in_9), .Clk(Clk), .En(decoder_1_out6));
  _8_bit_reg u_8_bit_reg_8 (.Din(Din), .out_4(in_10), .Clk(Clk), .En(decoder_1_out7));
  Decoder #(.select(3)) decoder_1 (
    .out0(decoder_1_out0), .out1(decoder_1_out1), .out2(decoder_1_out2), .out3(decoder_1_out3),
    .out4(decoder_1_out4), .out5(decoder_1_out5), .out6(decoder_1_out6), .out7(decoder_1_out7), .sel(in_12),
    .en(en));
  Multiplexer #(.select(3), .width(8), .enable("false")) multiplexer_1 (
    .in0(in_2), .in1(in_3), .in2(in_4), .in3(in_5), .in4(in_6), .in5(in_8), .in6(in_9), .in7(in_10),
    .out(out_14), .sel(in_7));
endmodule
