// Logisim project reg file.circ as structural Verilog: 2 circuits, main circuit main
module main (
  input  [3:0] Din,
  input  Cin,
  input  En,
  output [3:0] Dout
);

  D_Flip_Flop d_ff_1 (.clk(Cin), .D(Din[0]), .Q(Dout[0]), .en(En));  // open: Qn, preset, reset
  D_Flip_Flop d_ff_2 (.clk(Cin), .D(Din[1]), .Q(Dout[1]), .en(En));  // open: Qn, preset, reset
  D_Flip_Flop d_ff_3 (.clk(Cin), .D(Din[2]), .Q(Dout[2]), .en(En));  // open: Qn, preset, reset
  D_Flip_Flop d_ff_4 (.clk(Cin), .D(Din[3]), .Q(Dout[3]), .en(En));  // open: Qn, preset, reset
endmodule

module reg_file (
  input  [3:0] Din,
  input  Din_2,
  input  [1:0] Mux_sel,
  input  den,
  input  [1:0] Sel,
  output [3:0] out_6,
  output [3:0] out_7,
  output [3:0] out_8,
  output [3:0] out_9,
  output [3:0] out_10
);

  wire clock_1_out, decoder_1_out0, decoder_1_out1, decoder_1_out2, decoder_1_out3;

  Clock clock_1 (.out(clock_1_out));
  main R0 (.Din(Din), .Dout(out_6), .Cin(clock_1_out), .En(decoder_1_out0));
  main R1 (.Din(Din), .Dout(out_7), .Cin(clock_1_out), .En(decoder_1_out1));
  main R2 (.Din(Din), .Dout(out_9), .Cin(clock_1_out), .En(decoder_1_out2));
  main R3 (.Din(Din), .Dout(out_10), .Cin(clock_1_out), .En(decoder_1_out3));
  Decoder #(.select(2)) decoder_1 (
    .out0(decoder_1_out0), .out1(decoder_1_out1), .out2(decoder_1_out2), .out3(decoder_1_out3), .sel(Sel),
    .en(den));
  Multiplexer #(.select(2), .width(4)) multiplexer_1 (
    .in0(out_6), .in1(out_7), .in2(out_9), .in3(out_10), .out(out_8), .sel(Mux_sel), .en(Din_2));
endmodule
